# Fritzing sketch push-button-with-led (saved by Fritzing 0.9.3b)
breadboards: 1

parts:
  LED1 = LED - 5mm [color="Yellow (585nm)" package="5 mm [THT]"]
  R1 = Resistor [tolerance=±1% resistance=220 package=THT]
  Raspberry_Pi_1 = Raspberry Pi 3 [part_number=RPI-3-V1.2]
  S1 = Pushbutton [package="[THT]"]
  R2 = Resistor [tolerance=±1% resistance=1k package=THT]

nets:
  N1: LED1.cathode, R1.Pin_0
  N2: LED1.anode, Raspberry_Pi_1.GIPO18
  N3: R1.Pin_1, Raspberry_Pi_1.GND
  N4: Raspberry_Pi_1.3v3, R2.Pin_1
  N5: Raspberry_Pi_1.GIPO23, S1.Pin_1, S1.Pin_2
  N6: S1.Pin_3, S1.Pin_4, R2.Pin_0
