# Fritzing sketch transistor-with-led (saved by Fritzing 0.9.3b)
breadboards: 1

parts:
  LED1 = LED - 5mm [color="Yellow (585nm)" package="5 mm [THT]"]
  R1 = Resistor [tolerance=±1% resistance=22k package=THT]
  Raspberry_Pi_1 = Raspberry Pi 3 [part_number=RPI-3-V1.2]
  Q1 = NPN-Transistor [package="TO92 [THT]"]
  R2 = Resistor [tolerance=±5% resistance=220 package=THT]

nets:
  N1: LED1.cathode, R2.Pin_1
  N2: LED1.anode, Raspberry_Pi_1.5V
  N3: R1.Pin_0, Q1.B
  N4: R1.Pin_1, Raspberry_Pi_1.GIPO18
  N5: Raspberry_Pi_1.GND, Q1.E
  N6: Q1.C, R2.Pin_0

notes:
  using a 2N3904 and this tutorial: https://einhugur.com/blog/index.php/xojo-gpio/putting-the-gpio-pin-behind-transistor-to-get-more-current/
